# Fritzing sketch led-pumpkin (saved by Fritzing 1.0.1rc)
circuit board: 2.68824cm x 4.11027cm
breadboards: 1

parts:
  Part1 = ws2812b [package="smd 2812b"]
  R1 = Resistor [tolerance=±5% resistance=470 power=0.25W package=THT]
  D1 = Diode [package=diode-1n4148]
  J3 = Dagu DGServo 9g header (male) [package=THT]
  J2 = screw terminal, 2 pins
  C1 = Electrolytic Capacitor [capacitance=1mF voltage=35V package="200 mil [THT, electrolytic]"]
  WeMos_D1_Mini1 = WeMos D1 Mini

nets:
  N1: Part1.VDD, D1.C
  N2: Part1.DOUT, J3.Vcc
  GND: Part1.VSS, J3.gnd, J2.pin1, C1.-, WeMos_D1_Mini1.G
  N3: Part1.DIN, R1.Pin_0
  N4: R1.Pin_1, WeMos_D1_Mini1.RX
  N5: D1.A, J3.pulse, J2.pin2, C1.+, WeMos_D1_Mini1.5V
